# Fritzing sketch schematic (saved by Fritzing 0.9.3b)
breadboards: 1

parts:
  Part1 = Arduino Nano (Rev3.0)
  R1 = Resistor [tolerance=±5% resistance=10k package=THT]
  R2 = Resistor [tolerance=±5% resistance=1.8k package=THT]  # not connected
  U1 = mystery part, 2 pins [chip_label="Lead Acid"]
  Q1 = Basic FET N-Channel [package="TO220 [THT]"]
  R3 = Resistor [tolerance=±5% resistance=12k package=THT]
  LED1 = LED - 3mm [color="Red (633nm)" package="3 mm [THT]"]

nets:
  N1: Part1.GND, U1.pin2, Q1.source, R3.Pin_0, LED1.anode
  N2: Part1.D2, Q1.gate, R3.Pin_1
  N3: Part1.D4, R1.Pin_0
  N4: Q1.drain, LED1.cathode
